# Fritzing sketch SmartIrrigation_rev002 (saved by Fritzing 0.8.7b)
breadboards: 1

parts:
  Arduino_UNO = Arduino Uno (Rev3) - ICSP
  ESP8266_(_WIFI_Module_) = NodeMCU V1.0
  DHT1_(_humidity_Sensor_) = DHT22 Humidity and Temperature Sensor
  Soil_Moisture_Sensor = FC-28 Soil Hygrometer Module
  Soil_Moisture_Sensor_2 = FC-28 Soil Hygrometer Module - Probe
  KY-1 = Keyes Relay [package=THT]
  WATER_PUMP1 = water pump/motor  # not connected
  LED1 = LED - 5mm [color="Red (633nm)" package="5 mm [THT]"]
  LED2 = LED - 5mm [color="Green (565nm)" package="5 mm [THT]"]

nets:
  N1: Arduino_UNO.A0, Soil_Moisture_Sensor.AO
  5V: Arduino_UNO.5V, DHT1_(_humidity_Sensor_).VDD, Soil_Moisture_Sensor.VCC, KY-1.power
  GND: Arduino_UNO.GND, DHT1_(_humidity_Sensor_).GND, Soil_Moisture_Sensor.GND, KY-1.ground, LED1.anode, LED2.anode
  N2: Arduino_UNO.D8, DHT1_(_humidity_Sensor_).DATA
  N3: Arduino_UNO.D10_PWM/SS, LED2.cathode
  N4: Arduino_UNO.D11_PWM/MOSI, LED1.cathode
  N5: Arduino_UNO.D2, ESP8266_(_WIFI_Module_).TX
  N6: Arduino_UNO.D3_PWM, ESP8266_(_WIFI_Module_).RX
  N7: ESP8266_(_WIFI_Module_).D2, KY-1.signal
  N8: Soil_Moisture_Sensor.POS, Soil_Moisture_Sensor_2.POS
  N9: Soil_Moisture_Sensor.NEG, Soil_Moisture_Sensor_2.NEG
  N10: KY-1.C, KY-1.NO

custom parts:
  NodeMCU V1.0: ESP8266 based NodeMCU
  FC-28 Soil Hygrometer Module: The FC-28 is a soil hygrometer module that uses the Texas Instruments LM393 comparator chip to provide an analog measurement of soil humidity. The digital output is high when soil moisture is over a certain threshold, as determined by adjusting the potentiometer.
  FC-28 Soil Hygrometer Module - Probe: The FC-28 is a soil hygrometer module that uses the Texas Instruments LM393 comparator chip to provide an analog measurement of soil humidity.
  Keyes Relay: The Keyes 5V relay module is suitable for SCM development, home appliance control. It uses a 5V~12V TIL control signal which can control DC / AC signal.
  water pump/motor: WATER PUMP BY ARDUBLOCKTR
